// Logisim project Project1.circ as structural Verilog: 4 circuits, main circuit main
module main (
  input  in_1,
  input  in_2,
  input  in_3,
  input  in_4,
  input  Five,
  output N,
  output E,
  output [3:0] out_8
);

  wire fiveseven_1_a, fiveseven_1_b, fiveseven_1_c, fiveseven_1_d, fiveseven_1_e, fiveseven_1_f,
       fiveseven_1_g;

  Compare compare_1 (.X0(1'b1), .X1(1'b0), .X2(1'b1), .Y0(1'b1), .Y1(1'b1), .Y2(1'b1), .N(N), .E(E));
  Gray gray_1 (.B3(1'b1), .B2(1'b0), .B1(1'b1), .B0(1'b1), .G3(out_8[0]), .G2(out_8[1]), .G1(out_8[2]), .G0(out_8[3]));
  FiveSeven fiveseven_1 (
    .V(in_1), .W(in_2), .X(in_3), .Y(in_4), .Z(Five), .A(fiveseven_1_a), .B(fiveseven_1_b),
    .C(fiveseven_1_c), .D(fiveseven_1_d), .E(fiveseven_1_e), .F(fiveseven_1_f), .G(fiveseven_1_g));
  _7_Segment_Display u_7_segment_display_1 (
    .g(fiveseven_1_g), .f(fiveseven_1_f), .a(fiveseven_1_a), .b(fiveseven_1_b), .e(fiveseven_1_e),
    .d(fiveseven_1_d), .c(fiveseven_1_c));  // open: dp
endmodule

module Compare (
  input  X0,
  input  X1,
  input  X2,
  input  Y0,
  input  Y1,
  input  Y2,
  output N,
  output E
);

  wire and_1_out, and_2_out, and_3_out, and_4_out, and_5_out, xnor_1_out, xnor_2_out, xnor_3_out;

  and and_1 (and_1_out, ~X0, Y0);  // AND_Gate
  and and_2 (and_2_out, ~X1, Y1);  // AND_Gate
  and and_3 (and_3_out, ~X2, Y2);  // AND_Gate
  xnor xnor_1 (xnor_1_out, X0, Y0);
  xnor xnor_2 (xnor_2_out, X1, Y1);
  xnor xnor_3 (xnor_3_out, X2, Y2);
  and and_4 (and_4_out, and_1_out, xnor_2_out, xnor_3_out);
  and and_5 (and_5_out, and_2_out, xnor_3_out);
  or or_1 (N, and_4_out, and_5_out, and_3_out);
  and and_6 (E, xnor_1_out, xnor_2_out, xnor_3_out);
endmodule

module Gray (
  input  B3,
  input  B2,
  input  B1,
  input  B0,
  output G3,
  output G2,
  output G1,
  output G0
);

  wire and_1_out, and_2_out, and_3_out, and_4_out, and_5_out, and_6_out, and_7_out, and_8_out, and_9_out,
       and_10_out, and_11_out, not_1_out, not_2_out, not_4_out;

  not not_1 (not_1_out, B3);
  not not_2 (not_2_out, B2);
  not not_3 (G0, B1);
  not not_4 (not_4_out, B0);
  and and_1 (and_1_out, not_1_out, B2, B1, B0);
  and and_2 (and_2_out, B3, not_2_out);
  and and_3 (and_3_out, B3, G0);
  and and_4 (and_4_out, B3, not_4_out);
  and and_5 (and_5_out, not_1_out, B1, B0);
  and and_6 (and_6_out, not_1_out, B2);
  and and_7 (and_7_out, B3, not_2_out, G0);
  and and_8 (and_8_out, B3, not_2_out, not_4_out);
  and and_9 (and_9_out, not_2_out, B0);
  and and_10 (and_10_out, not_2_out, B1);
  and and_11 (and_11_out, B2, G0, not_4_out);
  or or_1 (G3, and_1_out, and_2_out, and_3_out, and_4_out);
  or or_2 (G2, and_5_out, and_6_out, and_7_out, and_8_out);
  or or_3 (G1, and_9_out, and_10_out, and_11_out);
endmodule

module FiveSeven (
  input  V,
  input  W,
  input  X,
  input  Y,
  input  Z,
  output A,
  output B,
  output C,
  output D,
  output E,
  output F,
  output G
);

  wire and_1_out, and_2_out, and_3_out, and_4_out, and_5_out, and_6_out, and_7_out, and_8_out, and_9_out,
       and_10_out, and_11_out, and_12_out, and_13_out, and_14_out, and_15_out, and_16_out, and_17_out,
       and_18_out, and_19_out, and_20_out, and_21_out, and_22_out, and_23_out, and_24_out, and_25_out,
       and_26_out, and_27_out, and_28_out, and_29_out, and_30_out, and_31_out, and_32_out, and_33_out,
       and_34_out, and_35_out, and_36_out, and_37_out, and_38_out, and_39_out, and_40_out, and_41_out,
       and_42_out, and_43_out, and_44_out, and_45_out, and_46_out, and_47_out, and_48_out, and_49_out,
       and_50_out, and_51_out, and_52_out, and_53_out, and_54_out, and_55_out, and_56_out, and_57_out,
       and_58_out, and_59_out, and_60_out, and_61_out, and_62_out, and_63_out, and_64_out, and_65_out,
       and_66_out, and_67_out, and_68_out, and_69_out, and_70_out, not_1_out, not_2_out, not_3_out,
       not_4_out, not_5_out;

  not not_1 (not_1_out, V);
  not not_2 (not_2_out, W);
  not not_3 (not_3_out, X);
  not not_4 (not_4_out, Y);
  not not_5 (not_5_out, Z);
  and and_1 (and_1_out, not_1_out, not_2_out, not_3_out, not_4_out);
  and and_2 (and_2_out, not_1_out, X, Y);
  and and_3 (and_3_out, not_1_out, W, Y);
  and and_4 (and_4_out, not_1_out, W, X);
  and and_5 (and_5_out, V, not_2_out, Y);
  and and_6 (and_6_out, V, not_2_out, X);
  and and_7 (and_7_out, V, W, not_3_out);
  and and_8 (and_8_out, W, X, not_4_out);
  and and_9 (and_9_out, X, Y);
  and and_10 (and_10_out, W, Y);
  and and_11 (and_11_out, W, X);
  and and_12 (and_12_out, V, Y);
  and and_13 (and_13_out, V, X);
  and and_14 (and_14_out, V, W);
  and and_15 (and_15_out, not_1_out, not_2_out, not_3_out);
  and and_16 (and_16_out, not_1_out, not_2_out, not_4_out);
  and and_17 (and_17_out, not_1_out, not_3_out, not_4_out);
  and and_18 (and_18_out, W, X, Y);
  and and_19 (and_19_out, not_2_out, not_3_out, not_4_out);
  and and_20 (and_20_out, V, X, Y);
  and and_21 (and_21_out, V, W, Y);
  and and_22 (and_22_out, V, W, X);
  and and_23 (and_23_out, not_1_out, not_2_out, not_3_out, not_4_out);
  and and_24 (and_24_out, not_1_out, not_2_out, not_3_out, Z);
  and and_25 (and_25_out, not_1_out, not_2_out, not_4_out, Z);
  and and_26 (and_26_out, not_1_out, not_3_out, not_4_out, Z);
  and and_27 (and_27_out, not_2_out, not_3_out, not_4_out, Z);
  and and_28 (and_28_out, not_1_out, X, Y, not_5_out);
  and and_29 (and_29_out, not_1_out, W, Y, not_5_out);
  and and_30 (and_30_out, not_1_out, W, X, not_5_out);
  and and_31 (and_31_out, not_1_out, W, X, Y);
  and and_32 (and_32_out, V, not_2_out, Y, not_5_out);
  and and_33 (and_33_out, V, not_2_out, X, not_5_out);
  and and_34 (and_34_out, V, not_2_out, X, Y);
  and and_35 (and_35_out, V, W, not_3_out, not_5_out);
  and and_36 (and_36_out, V, W, not_3_out, Y);
  and and_37 (and_37_out, V, X, not_4_out, not_5_out);
  and and_38 (and_38_out, V, W, X, not_4_out);
  and and_39 (and_39_out, V, X, Y, Z);
  and and_40 (and_40_out, not_1_out, not_2_out, not_3_out, not_4_out, not_5_out);
  and and_41 (and_41_out, not_1_out, not_2_out, not_3_out, Y, Z);
  and and_42 (and_42_out, not_1_out, not_2_out, X, not_4_out, Z);
  and and_43 (and_43_out, not_1_out, not_2_out, X, Y, not_5_out);
  and and_44 (and_44_out, not_1_out, W, not_3_out, not_4_out, Z);
  and and_45 (and_45_out, not_1_out, W, not_3_out, Y, not_5_out);
  and and_46 (and_46_out, not_1_out, W, X, not_4_out, not_5_out);
  and and_47 (and_47_out, not_1_out, W, X, Y, Z);
  and and_48 (and_48_out, V, not_2_out, not_3_out, not_4_out, Z);
  and and_49 (and_49_out, V, not_2_out, not_3_out, Y, not_5_out);
  and and_50 (and_50_out, V, not_2_out, X, not_4_out, not_5_out);
  and and_51 (and_51_out, V, not_2_out, X, Y, Z);
  and and_52 (and_52_out, V, W, not_3_out, not_4_out, not_5_out);
  and and_53 (and_53_out, V, W, not_3_out, Y, Z);
  and and_54 (and_54_out, V, W, X, not_4_out, Z);
  and and_55 (and_55_out, not_1_out, not_2_out, not_3_out, not_4_out);
  and and_56 (and_56_out, V, W, X, Y);
  and and_57 (and_57_out, not_1_out, not_2_out, not_3_out, Z);
  and and_58 (and_58_out, not_1_out, not_2_out, not_4_out, Z);
  and and_59 (and_59_out, X, Y, not_5_out);
  and and_60 (and_60_out, not_1_out, not_3_out, not_4_out, Z);
  and and_61 (and_61_out, W, Y, not_5_out);
  and and_62 (and_62_out, W, X, not_5_out);
  and and_63 (and_63_out, W, X, Y);
  and and_64 (and_64_out, not_2_out, not_3_out, not_4_out, Z);
  and and_65 (and_65_out, V, Y, not_5_out);
  and and_66 (and_66_out, V, X, not_5_out);
  and and_67 (and_67_out, V, X, Y);
  and and_68 (and_68_out, V, W, not_5_out);
  and and_69 (and_69_out, V, W, Y);
  and and_70 (and_70_out, V, W, X);
  or or_1 (A, and_1_out, Z, and_2_out, and_3_out, and_4_out, and_5_out, and_6_out, and_7_out, and_8_out);
  or or_2 (B, not_5_out, and_9_out, and_10_out, and_11_out, and_12_out, and_13_out, and_14_out);
  or or_3 (C, and_15_out, and_16_out, Z, and_17_out, and_18_out, and_19_out, and_20_out, and_21_out, and_22_out);
  or or_4 (F, and_55_out, Z, and_56_out);
  or or_5 (D, and_23_out, and_24_out, and_25_out, and_26_out, and_27_out, and_28_out, and_29_out, and_30_out, and_31_out, and_32_out, and_33_out, and_34_out, and_35_out, and_36_out, and_37_out, and_38_out, and_39_out);
  or or_6 (E, and_40_out, and_41_out, and_42_out, and_43_out, and_44_out, and_45_out, and_46_out, and_47_out, and_48_out, and_49_out, and_50_out, and_51_out, and_52_out, and_53_out, and_54_out);
  or or_7 (G, and_57_out, and_58_out, and_59_out, and_60_out, and_61_out, and_62_out, and_63_out, and_64_out, and_65_out, and_66_out, and_67_out, and_68_out, and_69_out, and_70_out);
endmodule
